# Fritzing sketch diagramaCircuitos2 (saved by Fritzing 0.9.3b)
breadboards: 1

parts:
  Componente1 = Arduino Uno (Rev3)
  LED1 = LED - 5mm [color="Red (633nm)" package="5 mm [THT]"]
  YL-83_-_Control_Board1 = YL-83 Rain Sensor - Control Board
  YL-83_-_Detection_Board1 = YL-83 Rain Sensor - Detection Board
  BT1 = Bluetooth HC-06u [package=THT]
  Componente2 = FC-28 Soil Hygrometer Module - Probe
  Componente3 = FC-28 Soil Hygrometer Module
  DHT1 = DHT11 Humitidy and Temperature Sensor
  LCD1 = LCD screen
  LCM1602_IIC1 = LCM1602 IIC [part_number="LCM1602 IIC" chip_label="LCM1602 IIC" package="DIP (Dual Inline) [THT]"]
  R1 = Resistor [tolerance=±5% resistance=220 package=THT]
  Power_plug1 = Power plug
  M2 = DC Motor
  F1 = Fan - Ventilador [package=THT]
  Water_Level_Sensor1 = Water Level Sensor
  Componente4 = Jtron 1 Channel Optoisolated Relay Module [package=relay]
  Componente5 = Jtron 1 Channel Optoisolated Relay Module [package=relay]
  J1 = Basic Servo
  J2 = Basic Servo

nets:
  N1: Componente1.A0, Componente3.AO
  N2: Componente1.A1, Water_Level_Sensor1.SIG
  N3: Componente1.A4/SDA, LCM1602_IIC1.SCL
  N4: Componente1.A5/SCL, LCM1602_IIC1.SDA
  N5: Componente1.D8, J1.pulse
  N6: Componente1.D9_PWM, J2.pulse
  N7: Componente1.D12/MISO, Componente4.IN1
  N8: Componente1.D13/SCK, Componente5.IN1
  N9: Componente1.D0/RX, BT1.TXD
  N10: Componente1.D1/TX, BT1.RXD
  N11: Componente1.D2, DHT1.DATA
  N12: Componente1.D3_PWM, LED1.anode
  N13: Componente1.D4, YL-83_-_Control_Board1.DO
  GND: Componente1.GND, YL-83_-_Control_Board1.GND, BT1.GND, Componente3.GND, DHT1.GND, LCM1602_IIC1.GND, R1.Pin_1, Power_plug1.GND, M2.pin_2, F1.GND, Water_Level_Sensor1.GND, Componente4.GND, Componente5.GND, J1.gnd
  N14: LED1.cathode, R1.Pin_0
  VCC: YL-83_-_Control_Board1.VCC, BT1.VCC, Componente3.VCC, DHT1.VDD, LCM1602_IIC1.VCC, Power_plug1.VCC, Water_Level_Sensor1.VCC, Componente4.VCC, Componente4.NO, Componente5.VCC, Componente5.NO, J1.vcc, J2.vcc
  N15: YL-83_-_Control_Board1.POS, YL-83_-_Detection_Board1.POS
  N16: YL-83_-_Control_Board1.NEG, YL-83_-_Detection_Board1.NEG
  N17: Componente2.POS, Componente3.POS
  N18: Componente2.NEG, Componente3.NEG
  VSS: LCD1.VSS, LCM1602_IIC1.VSS
  VDD: LCD1.VDD, LCM1602_IIC1.VDD
  N19: LCD1.V0, LCM1602_IIC1.V0
  N20: LCD1.RS, LCM1602_IIC1.RS
  N21: LCD1.R/W, LCM1602_IIC1.RW
  N22: LCD1.E, LCM1602_IIC1.E
  N23: LCD1.DB0, LCM1602_IIC1.D0
  N24: LCD1.DB1, LCM1602_IIC1.D1
  N25: LCD1.DB2, LCM1602_IIC1.D2
  N26: LCD1.DB3, LCM1602_IIC1.D3
  N27: LCD1.DB4, LCM1602_IIC1.D4
  N28: LCD1.DB5, LCM1602_IIC1.D5
  N29: LCD1.DB6, LCM1602_IIC1.D6
  N30: LCD1.DB7, LCM1602_IIC1.D7
  N31: LCD1.LED+, LCM1602_IIC1.A
  N32: LCD1.LED-, LCM1602_IIC1.K
  N33: M2.pin_1, Componente5.MAIN

notes:
  Bomba de agua
  Fuente 5v
  2A
  Modulo Bluetooth hc-06
  Servo 1
  Servo 2
  Modulos Rele 1 canal
  Cooler
  Display 16x02
  Sensor temperatura
  Sensor lluvia por goteo
  Sensor Humedad de la Tierra
  Sensor Nivel
  de agua

custom parts:
  YL-83 Rain Sensor - Control Board: The YL-83 is a rain sensor that has more resistance when dry and less resistance when wet. The module runs at 5V.
  YL-83 Rain Sensor - Detection Board: The YL-83 is a rain sensor that has more resistance when dry and less resistance when wet. The module runs at 5V.
  Bluetooth HC-06u: Bluetooth HC-06 - face up, pins down 16.5mm x 37.5mm PCB
  FC-28 Soil Hygrometer Module - Probe: The FC-28 is a soil hygrometer module that uses the Texas Instruments LM393 comparator chip to provide an analog measurement of soil humidity.
  FC-28 Soil Hygrometer Module: The FC-28 is a soil hygrometer module that uses the Texas Instruments LM393 comparator chip to provide an analog measurement of soil humidity. The digital output is high when soil moisture is over a certain threshold, as determined by adjusting the potentiometer.
  DHT11 Humitidy and Temperature Sensor: DHT11 Humidity and Temperature Sensor
  LCM1602 IIC: I2C-Module to use a 1602 or 2004 LCD on with the wire.h libory Serial LCD Modul
  Fan - Ventilador: Ventilador de 2 pines, se encuentra comunmente en computadoras de escritorio
  Water Level Sensor: A water level sensor. This sensor operates at 3V to 5V. The Sig (signal) pin outputs an analogue signal that is in proportion to the amount of water in contact with the sensor.
